# Fritzing sketch 3DLidarScanner-v1 (saved by Fritzing 0.9.10b)
breadboards: 1

parts:
  Power_plug1 = Power plug
  Part2 = LIDAR-TFMini-S
  J1 = Basic Servo
  M1 = ESP32-C3-DevKitM-1 [part_number=ESP32-C3-DevKitM-1]
  J2 = Basic Servo
  S3 = Pushbutton [package="[THT]"]

nets:
  GND: Power_plug1.GND, Part2.GND, J1.gnd, M1.GND-12, M1.GND-15, M1.GND-30, J2.gnd
  VCC: Power_plug1.VCC, Part2.+5V, J1.vcc, J2.vcc
  N1: Part2.RXD/SDA, M1.4
  N2: Part2.TXD/SCL, M1.5
  N3: J1.pulse, M1.19
  N4: M1.18, J2.pulse
  N5: S3.Pin_1, S3.Pin_2, S3.Pin_3, S3.Pin_4

custom parts:
  LIDAR-TFMini-S: Benewake TFmini-S LIDAR sensor https://www.mouser.com/datasheet/2/1099/Benewake_10152020_TFmini_S-1954051.pdf
  ESP32-C3-DevKitM-1: The DOIT Esp32 DevKit v1 is one of the development board created by DOIT to evaluate the ESP-WROOM-32 module. It is based on the ESP32 microcontroller that boasts Wifi, Bluetooth, Ethernet and Low Power support all in a single chip. (vanepp) Feb 2021: converted to ESP32-C3-DevKitM-1. This chip is 30pins long (2 x15) and 11 pins width.
